# Fritzing sketch RFduino_LedBtn (saved by Fritzing 0.8.5b)
breadboards: 1

parts:
  RFduino1 = RFduino
  R2 = Resistor [tolerance=±5% resistance=10k package=THT]
  Button_A = Pushbutton [package="[THT]"]
  R3 = Resistor [tolerance=±5% resistance=220 package=THT]
  LED2 = LED - 5mm [color="Green (570nm)" package="5 mm [THT]"]
  R7 = Resistor [tolerance=±5% resistance=220 package=THT]

nets:
  N1: RFduino1.gnd, R2.Pin_0, LED2.cathode
  N2: RFduino1.vin, Button_A.Pin_3, Button_A.Pin_4
  N3: RFduino1.gpio3, R7.Pin_1
  N4: RFduino1.gpio5, R3.Pin_1
  N5: R2.Pin_1, Button_A.Pin_1, Button_A.Pin_2, R3.Pin_0
  N6: LED2.anode, R7.Pin_0

custom parts:
  RFduino: RFduino board
